# Fritzing sketch Circuit (saved by Fritzing 0.8.5b)
breadboards: 1

parts:
  Raspberry_Pi_B_rev1 = Raspberry Pi B rev1
  R1 = Resistor [tolerance=±5% resistance=10k package=THT]
  M1 = DC Motor
  S1 = Square Pushbutton
  J1 = Power Jack [package=power_jack_combo]
  l298n = L298 [package=multiwatt15]

nets (from the breadboard view):
  N1: Raspberry_Pi_B_rev1.5V, R1.Pin_1, l298n.VLS
  GND: Raspberry_Pi_B_rev1.GND, S1.leg1, J1.GND, l298n.CSA, l298n.GND, l298n.CSB
  N2: Raspberry_Pi_B_rev1.GPIO_23, l298n.IN1
  N3: Raspberry_Pi_B_rev1.GPIO_17, R1.Pin_0, S1.leg0
  N4: Raspberry_Pi_B_rev1.GPIO_24, l298n.IN2
  N5: Raspberry_Pi_B_rev1.GPIO_25, l298n.ENA
  N6: M1.pin_1, l298n.OUT2
  N7: M1.pin_2, l298n.OUT1
  N8: J1.PWR, l298n.VS

notes:
  Note: This is from what I can remember and there is a good chance it is wrong
